# Fritzing sketch PW (saved by Fritzing 0.8.7b)
breadboards: 1

parts:
  U1 = Module 4 Relais 5V [package="Module 4 Relais 5V"]
  Componente2 = FC-28 Soil Hygrometer Module
  Componente3 = FC-28 Soil Hygrometer Module - Probe
  LED2 = smd LED [color="Blue (470nm)" package="0603 [SMD]"]
  R5 = Resistor [tolerance=±5% resistance=220 package="0603 [SMD]"]
  Componente1 = Arduino Uno (Rev3) - ICSP
  Part1 = KY-015 Temperature & Humidity Sensor Module [package="Breakout board"]
  R6 = PHOTOCELL [package=photocell-kit]
  R7 = Resistor [tolerance=±5% resistance=1k package="0603 [SMD]"]
  LED3 = smd LED [color="Red (660nm)" package="0603 [SMD]"]
  R8 = Resistor [tolerance=±5% resistance=220 package="0603 [SMD]"]
  Water_Level_Sensor2 = Water Level Sensor [package=board]
  U3 = WS2812 RGB LED strip
  MOTOR2 = 28BYJ-48 Stepper Motor
  X2 = X113647 Stepper Driver Board [part_number=X113647 package=board]
  WATER_PUMP1 = water pump/motor  # not connected
  U4 = Module 4 Relais 5V [package="Module 4 Relais 5V"]
  Componente4 = FC-28 Soil Hygrometer Module
  Componente5 = FC-28 Soil Hygrometer Module - Probe
  Componente6 = FC-28 Soil Hygrometer Module
  Componente7 = FC-28 Soil Hygrometer Module - Probe
  WATER_PUMP2 = water pump/motor  # not connected
  WATER_PUMP3 = water pump/motor  # not connected
  VCC2 = Battery block 9V
  Part3 = Bluetooth HC-05 Macho
  BAT1 = BC9VPC [package=bc9vpc]  # not connected

nets:
  VCC: U1.VCC, Componente2.VCC, Componente1.5V, Part1.Vin, R6.P$2, Water_Level_Sensor2.VCC, U4.VCC, Componente4.VCC, Componente6.VCC, Part3.VCC
  GND: U1.GND, Componente2.GND, LED2.cathode, Componente1.GND, Part1.-, R7.Pin_0, LED3.cathode, Water_Level_Sensor2.GND, X2.GND, U4.GND, Componente4.GND, Componente6.GND, Part3.GND
  N1: U1.IN1, Componente1.D5_PWM
  N2: U1.IN2, Componente1.D6_PWM
  N3: U1.IN3, Componente1.D7
  N4: U1.IN4, Componente1.D8
  N5: U1.K1-NF, U1.K2-NF, U1.K3-NF, U1.K4-NF, U4.K1-NF, VCC2.+
  N6: U1.K1-NO, U3.VCC
  N7: Componente2.AO, Componente1.A3
  N8: Componente2.POS, Componente3.POS
  N9: Componente2.NEG, Componente3.NEG
  N10: LED2.anode, R5.Pin_1
  N11: R5.Pin_0, Componente1.D4
  N12: Componente1.A0, R6.P$1, R7.Pin_1
  N13: Componente1.A2, Componente6.AO
  N14: Componente1.A4/SDA, Componente4.AO
  N15: Componente1.A5/SCL, Water_Level_Sensor2.SIG
  N16: Componente1.ICSP_MISO, Componente1.D12/MISO, X2.IN2
  N17: Componente1.ICSP_MOSI, Componente1.D11_PWM/MOSI, X2.IN3
  N18: Componente1.D9_PWM, U4.IN1
  N19: Componente1.D10_PWM/SS, X2.IN4
  N20: Componente1.D13/SCK, X2.IN1
  N21: Componente1.D0/RX, Part3.TXD
  N22: Componente1.D1/TX, Part3.RXD
  N23: Componente1.D2, Part1.S
  N24: Componente1.D3_PWM, R8.Pin_0
  N25: LED3.anode, R8.Pin_1
  N26: MOTOR2.BLUE, X2.BLUE
  N27: MOTOR2.PINK, X2.PINK
  N28: MOTOR2.RED, X2.YELLOW
  N29: MOTOR2.ORANGE, X2.ORANGE
  N30: MOTOR2.YELLOW, X2.RED
  N31: X2.+V, U4.K1-NO
  N32: Componente4.POS, Componente5.POS
  N33: Componente4.NEG, Componente5.NEG
  N34: Componente6.POS, Componente7.POS
  N35: Componente6.NEG, Componente7.NEG

custom parts:
  Module 4 Relais 5V: Module 4 Relais 5V 4x SPD-06VDC-SD-C
  FC-28 Soil Hygrometer Module: The FC-28 is a soil hygrometer module that uses the Texas Instruments LM393 comparator chip to provide an analog measurement of soil humidity. The digital output is high when soil moisture is over a certain threshold, as determined by adjusting the potentiometer.
  FC-28 Soil Hygrometer Module - Probe: The FC-28 is a soil hygrometer module that uses the Texas Instruments LM393 comparator chip to provide an analog measurement of soil humidity.
  KY-015 Temperature & Humidity Sensor Module: DH-11 temperature and humidity sensor in KEYES KY-015 module, provides a low-latency serial interface to measure humidity and temperature.
  Water Level Sensor: A water level sensor. This sensor operates at 3V to 5V. The Sig (signal) pin outputs an analogue signal that is in proportion to the amount of water in contact with the sensor.
  WS2812 RGB LED strip: WS2812 strip
  28BYJ-48 Stepper Motor: 28BYJ-48 gear-reduction stepper motor (small)
  X113647 Stepper Driver Board: A common stepper motor driver board based on ULN2003APG darlington array
  water pump/motor: WATER PUMP BY ARDUBLOCKTR
